# Fritzing sketch Sensor de Re (saved by Fritzing 0.7.12b)
breadboards: 1

parts:
  Arduino1 = Arduino
  Part1 = SRF05 Ultrasonic Rangefinder

nets:
  N1: Arduino1.D13, Part1.Trig
  N2: Arduino1.D12, Part1.Echo
